// Logisim project Contador (12h).circ as structural Verilog: 1 circuit, main circuit main
// CLK
module main (
  input  in_1,
  input  in_2,
  input  in_3,
  input  in_4,
  input  in_5,
  input  in_6,
  output out_7,
  output out_8,
  output out_9,
  output out_10,
  output out_11,
  output out_12,
  output out_13,
  output out_14,
  output out_15,
  output out_16,
  output out_17,
  output out_18,
  output out_19,
  output out_20,
  output out_21,
  output out_22,
  output out_23,
  output out_24,
  output out_25,
  output out_26,
  output out_27,
  output out_28,
  output out_29,
  output out_30
);

  wire and_1_out, and_2_out, and_3_out, and_4_out, and_5_out, and_6_out, and_7_out, CLK_out, or_1_out;

  and and_1 (and_1_out, out_26, out_29);
  J_K_Flip_Flop #(.trigger("falling")) j_k_ff_1 (
    .J(in_5), .clk(out_24), .K(in_5), .Q(out_23), .reset(and_1_out));  // open: Qn, preset, en
  J_K_Flip_Flop #(.trigger("falling")) j_k_ff_2 (
    .J(in_5), .clk(out_26), .K(in_5), .Q(out_24), .reset(and_1_out));  // open: Qn, preset, en
  J_K_Flip_Flop #(.trigger("falling")) j_k_ff_3 (
    .J(in_5), .clk(out_26), .K(in_5), .Q(out_25), .reset(and_1_out));  // open: Qn, preset, en
  Hex_Digit_Display hex_digit_display_1 (.value({out_23, out_24, out_25, out_26}));  // open: dp
  J_K_Flip_Flop #(.trigger("falling")) j_k_ff_4 (
    .J(in_5), .clk(out_27), .K(in_5), .Q(out_26), .reset(and_1_out));  // open: Qn, preset, en
  LED led_1 (.in(1'b1));
  LED led_2 (.in(1'b1));
  Hex_Digit_Display hex_digit_display_2 (.value({out_27, out_28, out_29, out_30}));  // open: dp
  and and_2 (and_2_out, out_27, out_29);
  and and_3 (and_3_out, out_29, and_1_out);
  Hex_Digit_Display hex_digit_display_3 (.value({out_11, out_12, out_13, out_14}));  // open: dp
  Hex_Digit_Display hex_digit_display_4 (.value({out_7, out_8, out_9, out_10}));  // open: dp
  J_K_Flip_Flop #(.trigger("falling")) j_k_ff_5 (
    .J(in_6), .clk(out_28), .K(in_6), .Q(out_27), .reset(or_1_out));  // open: Qn, preset, en
  or or_1 (or_1_out, and_2_out, and_3_out);
  LED led_3 (.in(1'b1));
  LED led_4 (.in(1'b1));
  Hex_Digit_Display hex_digit_display_5 (.value({out_15, out_16, out_17, out_18}));  // open: dp
  J_K_Flip_Flop #(.trigger("falling")) j_k_ff_6 (
    .J(in_6), .clk(out_29), .K(in_6), .Q(out_28), .reset(or_1_out));  // open: Qn, preset, en
  Hex_Digit_Display hex_digit_display_6 (.value({out_19, out_20, out_21, out_22}));  // open: dp
  J_K_Flip_Flop #(.trigger("falling")) j_k_ff_7 (
    .J(in_6), .clk(out_30), .K(in_6), .Q(out_29), .reset(or_1_out));  // open: Qn, preset, en
  J_K_Flip_Flop #(.trigger("falling")) j_k_ff_8 (
    .J(in_6), .clk(out_9), .K(in_6), .Q(out_30), .reset(or_1_out));  // open: Qn, preset, en
  and and_4 (and_4_out, out_9, out_8);
  J_K_Flip_Flop #(.trigger("falling")) j_k_ff_9 (
    .J(in_1), .clk(out_8), .K(in_1), .Q(out_7), .reset(and_4_out));  // open: Qn, preset, en
  J_K_Flip_Flop #(.trigger("falling")) j_k_ff_10 (
    .J(in_1), .clk(out_9), .K(in_1), .Q(out_8), .reset(and_4_out));  // open: Qn, preset, en
  J_K_Flip_Flop #(.trigger("falling")) j_k_ff_11 (
    .J(in_1), .clk(out_10), .K(in_1), .Q(out_9), .reset(and_4_out));  // open: Qn, preset, en
  J_K_Flip_Flop #(.trigger("falling")) j_k_ff_12 (
    .J(in_1), .clk(out_11), .K(in_1), .Q(out_10), .reset(and_4_out));  // open: Qn, preset, en
  J_K_Flip_Flop #(.trigger("falling")) j_k_ff_13 (
    .J(in_2), .clk(out_12), .K(in_2), .Q(out_11), .reset(and_5_out));  // open: Qn, preset, en
  and and_5 (and_5_out, out_11, out_13);
  J_K_Flip_Flop #(.trigger("falling")) j_k_ff_14 (
    .J(in_2), .clk(out_13), .K(in_2), .Q(out_12), .reset(and_5_out));  // open: Qn, preset, en
  J_K_Flip_Flop #(.trigger("falling")) j_k_ff_15 (
    .J(in_2), .clk(out_14), .K(in_2), .Q(out_13), .reset(and_5_out));  // open: Qn, preset, en
  J_K_Flip_Flop #(.trigger("falling")) j_k_ff_16 (
    .J(in_2), .clk(out_17), .K(in_2), .Q(out_14), .reset(and_5_out));  // open: Qn, preset, en
  and and_6 (and_6_out, out_17, out_16);
  J_K_Flip_Flop #(.trigger("falling")) j_k_ff_17 (
    .J(in_3), .clk(out_16), .K(in_3), .Q(out_15), .reset(and_6_out));  // open: Qn, preset, en
  J_K_Flip_Flop #(.trigger("falling")) j_k_ff_18 (
    .J(in_3), .clk(out_17), .K(in_3), .Q(out_16), .reset(and_6_out));  // open: Qn, preset, en
  J_K_Flip_Flop #(.trigger("falling")) j_k_ff_19 (
    .J(in_3), .clk(out_18), .K(in_3), .Q(out_17), .reset(and_6_out));  // open: Qn, preset, en
  J_K_Flip_Flop #(.trigger("falling")) j_k_ff_20 (
    .J(in_3), .clk(out_19), .K(in_3), .Q(out_18), .reset(and_6_out));  // open: Qn, preset, en
  J_K_Flip_Flop #(.trigger("falling")) j_k_ff_21 (
    .J(in_4), .clk(out_20), .K(in_4), .Q(out_19), .reset(and_7_out));  // open: Qn, preset, en
  and and_7 (and_7_out, out_19, out_21);
  J_K_Flip_Flop #(.trigger("falling")) j_k_ff_22 (
    .J(in_4), .clk(out_21), .K(in_4), .Q(out_20), .reset(and_7_out));  // open: Qn, preset, en
  J_K_Flip_Flop #(.trigger("falling")) j_k_ff_23 (
    .J(in_4), .clk(out_22), .K(in_4), .Q(out_21), .reset(and_7_out));  // open: Qn, preset, en
  Clock CLK (.out(CLK_out));
  J_K_Flip_Flop #(.trigger("falling")) j_k_ff_24 (
    .J(in_4), .clk(CLK_out), .K(in_4), .Q(out_22), .reset(and_7_out));  // open: Qn, preset, en
endmodule
